// Logisim project logisim_project_pdip40.circ as structural Verilog: 2 circuits, main circuit main
module main (
  input  in_1
);

  wire and_1_out, and_2_out, and_3_out, and_4_out, and_5_out, and_6_out, and_7_out, and_8_out, button_1_out,
       button_2_out, clock_1_out, clock_2_out, clock_3_out, clock_4_out, clock_5_out, clock_6_out,
       decoder_1_out0, decoder_1_out1, decoder_3_out0, decoder_3_out1, decoder_3_out2, IO0, IO1, IRQB,
       not_1_out, not_2_out, not_5_out, or_2_out, RAMEN, READ, RES, ROMEN, SERIAL, VIDEO,
       w65c02s_pdip_40_1_p5, WRITE;
  wire [0:0] keyboard_1_avail;
  wire [6:0] controlled_buffer_2_out, keyboard_1_data;
  wire [7:0] D, register_1_q, register_2_q, rom_1_data;
  wire [7:7] pull_resistor_7_node;
  wire [14:0] A;

  Clock clock_1 (.out(clock_1_out));
  and and_1 (and_1_out, READ, RAMEN);
  and and_2 (and_2_out, WRITE, RAMEN);
  Pull_Resistor pull_resistor_1 (.node(IRQB));
  Button button_1 (.out(button_1_out));
  ROM #(.addrWidth(15)) rom_1 (.addr(A), .data(rom_1_data));
  RAM #(.addrWidth(14), .clearpin("true"), .databus("bidir")) ram_1 (
    .addr(A[13:0]), .we(and_2_out), .oe(and_1_out), .clk(clock_1_out), .clr(in_1));  // open: data
  Clock clock_2 (.out(clock_2_out));
  and and_3 (and_3_out, IRQB, not_1_out);
  not not_1 (not_1_out, button_1_out);
  not not_2 (not_2_out, button_2_out);
  Button button_2 (.out(button_2_out));
  Pull_Resistor pull_resistor_2 (.node(A));
  // W65C02S__PDIP_40 w65c02s_pdip_40_1: pin names not known; wires that end beside it: 1'b1, and_3_out, not_2_out, 1'b1, w65c02s_pdip_40_1_p5, 1'b1, clock_2_out, READ, ROMEN, A[14], A[13], A[12], 1'b0
  not not_3 (w65c02s_pdip_40_1_p5, RES);
  Pull_Resistor #(.pull(1)) pull_resistor_3 (.node(READ));
  Pull_Resistor pull_resistor_4 (.node(D));
  assign D = ROMEN ? rom_1_data : 8'bz;  // Controlled_Buffer controlled_buffer_1
  not not_4 (WRITE, READ);
  Pull_Resistor pull_resistor_5 (.node(ROMEN));
  not not_5 (not_5_out, ROMEN);
  Decoder #(.select(2)) decoder_1 (
    .out0(decoder_1_out0), .out1(decoder_1_out1), .out2(IO0), .out3(IO1), .sel(A[14:13]), .en(not_5_out));
  or or_1 (RAMEN, decoder_1_out0, decoder_1_out1);
  Decoder #(.select(3)) decoder_2 (
    .out0(SERIAL), .out1(VIDEO), .sel(A[12:10]), .en(IO0));  // open: out2, out3, out4, out5, out6, out7
  Pull_Resistor pull_resistor_6 (.node(D[7]));
  assign controlled_buffer_2_out = and_4_out ? D[6:0] : 7'bz;  // Controlled_Buffer controlled_buffer_2
  Clock clock_3 (.out(clock_3_out));
  TTY #(.cols(40), .rows(16)) tty_1 (.data(controlled_buffer_2_out), .clk(clock_3_out), .we(and_4_out), .clr(or_2_out));
  and and_4 (and_4_out, decoder_3_out0, WRITE);
  Keyboard #(.buflen(64)) keyboard_1 (
    .clk(clock_3_out), .re(and_5_out), .clr(or_2_out), .avail(keyboard_1_avail[0]), .data(keyboard_1_data));
  or or_2 (or_2_out, RES, register_2_q[7]);
  and and_5 (and_5_out, decoder_3_out0, READ);
  Pull_Resistor pull_resistor_7 (.node(pull_resistor_7_node[7]));
  Register register_1 (
    .D({pull_resistor_7_node[7], keyboard_1_data}), .en(and_5_out), .clk(clock_4_out), .Q(register_1_q));  // open: clr
  Clock clock_4 (.out(clock_4_out));
  assign D = and_5_out ? register_1_q : 8'bz;  // Controlled_Buffer controlled_buffer_3
  Register register_2 (.D(D), .en(and_6_out), .clk(clock_5_out), .Q(register_2_q), .clr(1'b0));
  and and_6 (and_6_out, WRITE, decoder_3_out1);
  Clock clock_5 (.out(clock_5_out));
  Pull_Resistor pull_resistor_8 (.node(SERIAL));
  Decoder #(.select(2)) decoder_3 (
    .out0(decoder_3_out0), .out1(decoder_3_out1), .out2(decoder_3_out2), .sel(A[1:0]), .en(SERIAL));  // open: out3
  video_controller video_controller_1 (
    .RESET(RES), .WRITE(and_7_out), .RS(A[2:0]), .DATAIN(D), .CLK(clock_6_out));  // open: SCREEN_CLK, X, Y, COLOR, SCREEN_RESET, SCREEN_WRITE
  // RGB_Video #(.cursor("No Cursor"), .scale(1), .width(256)) rgb_video_1: pin names not known
  and and_7 (and_7_out, WRITE, VIDEO);
  Button button_3 (.out(RES));
  assign D = and_8_out ? {{7{1'b0}}, keyboard_1_avail[0]} : 8'bz;  // Controlled_Buffer controlled_buffer_4
  and and_8 (and_8_out, decoder_3_out2, READ);
  Clock clock_6 (.out(clock_6_out));

  // Notes on the sheet:
  //   contents of rom_1 (hex, n*v repeats v):
  //   a2 0 bd 0 a0 c9 0 f0 7 8d 0 40 e8 4c 2 80 4c 0 ff 8173*0 49 27 6d 20 6c 6f 63 61 74 65 64 20 61 74
  //   20 24 32 30 30 30 20 69 6e 20 74 68 65 20 52 4f 4d 20 65 64 69 74 20 6d 65 20 74 6f 20 79 6f 75 72
  //   20 6c 69 6b 69 6e 67 21 20 4a 75 73 74 20 6c 65 61 76 65 20 61 20 24 30 30 20 61 74 20 74 68 65 20
  //   65 6e 64 20 73 6f 20 49 20 6b 6e 6f 77 20 74 68 65 20 73 74 72 69 6e 67 20 65 6e 64 65 64 2e 20 44
  //   72 6f 70 70 69 6e 67 20 69 6e 74 6f 20 77 6f 7a 6d 6f 6e 2e 2e 2e a 24184*0 a9 1b c9 8 f0 13 c9 1b
  //   f0 3 c8 10 f a9 5c 20 e5 ff a9 a 20 e5 ff a0 1 88 30 f6 ad 2 40 29 1 f0 f9 ad 0 40 99 0 2 20 e5 ff
  //   c9 a d0 d2 a0 ff a9 0 aa a a 85 2b c8 b9 0 2 c9 a f0 d1 c9 2e 90 f4 f0 ee c9 3a f0 eb c9 52 f0 3b 86
  //   28 86 29 84 2a b9 0 2 49 30 c9 a 90 6 69 88 c9 fa 90 11 4*a a2 4 a 26 28 26 29 ca d0 f8 c8 d0 e0 c4
  //   2a f0 94 24 2b 50 10 a5 28 81 26 e6 26 d0 b5 e6 27 4c 3a ff 6c 24 0 30 2b a2 2 b5 27 95 25 95 23 ca
  //   d0 f7 d0 14 a9 a 20 e5 ff a5 25 20 d2 ff a5 24 20 d2 ff a9 3a 20 e5 ff a9 20 20 e5 ff a1 24 20 d2 ff
  //   86 2b a5 24 c5 28 a5 25 e5 29 b0 c1 e6 24 d0 2 e6 25 a5 24 29 7 10 c8 48 4*4a 20 db ff 68 29 f 9 30
  //   c9 3a 90 2 69 6 48 8d 0 40 68 60 16*0 f 0 80
  //   serial range: $4000-$43FF
  //   Video range: $4400-$47FF
endmodule

module video_controller (
  input  WRITE,
  input  [2:0] RS,
  input  [7:0] DATAIN,
  input  CLK,
  input  RESET,
  output SCREEN_CLK,
  output [7:0] X,
  output [6:0] Y,
  output [23:0] COLOR,
  output SCREEN_WRITE,
  output SCREEN_RESET
);

  wire d_ff_1_q, d_ff_2_q, decoder_1_out0, decoder_1_out1, decoder_1_out2, decoder_1_out3, decoder_1_out4,
       decoder_1_out5;
  wire [7:0] register_6_q;
  wire [7:7] register_2_q;

  Decoder #(.select(3)) decoder_1 (
    .out0(decoder_1_out0), .out1(decoder_1_out1), .out2(decoder_1_out2), .out3(decoder_1_out3),
    .out4(decoder_1_out4), .out5(decoder_1_out5), .sel(RS), .en(WRITE));  // open: out6, out7
  Register register_1 (.D(DATAIN), .en(decoder_1_out0), .clk(CLK), .Q(X), .clr(SCREEN_RESET));
  Register register_2 (.D(DATAIN), .en(decoder_1_out1), .clk(CLK), .Q({register_2_q[7], Y}), .clr(SCREEN_RESET));
  Register register_3 (.D(DATAIN), .en(decoder_1_out2), .clk(CLK), .Q(COLOR[7:0]), .clr(SCREEN_RESET));
  Register register_4 (.D(DATAIN), .en(decoder_1_out3), .clk(CLK), .Q(COLOR[15:8]), .clr(SCREEN_RESET));
  Register register_5 (.D(DATAIN), .en(decoder_1_out4), .clk(CLK), .Q(COLOR[23:16]), .clr(SCREEN_RESET));
  Register register_6 (.D(DATAIN), .en(decoder_1_out5), .clk(CLK), .Q(register_6_q), .clr(RESET));
  Pull_Resistor pull_resistor_1 (.node(register_2_q[7]));
  D_Flip_Flop d_ff_1 (.D(register_6_q[0]), .clk(CLK), .Q(d_ff_1_q), .reset(RESET));  // open: Qn, preset
  D_Flip_Flop d_ff_2 (.D(register_6_q[1]), .clk(CLK), .Q(d_ff_2_q), .reset(RESET));  // open: Qn, preset
  xor xor_1 (SCREEN_WRITE, register_6_q[0], d_ff_1_q);
  xor xor_2 (SCREEN_RESET, register_6_q[1], d_ff_2_q);

  assign SCREEN_CLK = CLK;
endmodule
